// Logisim project seven_segment_driver.circ as structural Verilog: 1 circuit, main circuit main
module main (
);

  wire and_1_out, and_2_out, and_3_out, and_4_out, and_5_out, and_6_out, and_7_out, and_8_out, and_9_out,
       and_10_out, and_11_out, and_12_out, and_13_out, and_14_out, and_15_out, and_16_out, and_17_out,
       clock_out, not_4_out, or_1_out, or_2_out, or_3_out, or_4_out, or_5_out, or_6_out, or_7_out, or_8_out,
       Q0, Q0_t, Q1, Q1_t, Q2, Q2_t, xor_1_out, xor_2_out;

  D_Flip_Flop D2 (.clk(clock_out), .D(xor_2_out), .Q(Q2));  // open: Qn, preset, en, reset
  not not_1 (Q2_t, Q2);
  Clock clock (.out(clock_out));
  not not_2 (Q1_t, Q1);
  and and_1 (and_1_out, Q0_t, Q2_t);
  and and_2 (and_2_out, Q0, Q2);
  and and_3 (and_3_out, Q0_t, Q1_t);
  and and_4 (and_4_out, Q0, Q1);
  and and_5 (and_5_out, Q1_t, Q2);
  and and_6 (and_6_out, Q0_t, Q2);
  and and_7 (and_7_out, Q2_t, Q1);
  and and_8 (and_8_out, Q0_t, Q1);
  and and_9 (and_9_out, Q1_t, Q2, Q0);
  D_Flip_Flop D1 (.clk(clock_out), .D(xor_1_out), .Q(Q1));  // open: Qn, preset, en, reset
  D_Flip_Flop D0 (.clk(clock_out), .D(not_4_out), .Q(Q0));  // open: Qn, preset, en, reset
  or or_1 (or_1_out, and_1_out, and_2_out, Q1);
  or or_2 (or_2_out, and_3_out, Q2_t, and_4_out);
  or or_3 (or_3_out, and_5_out, and_3_out, and_6_out);
  or or_4 (or_4_out, and_5_out, and_6_out, and_7_out);
  or or_5 (or_5_out, Q2, Q1_t, Q0);
  or or_6 (or_6_out, and_1_out, and_8_out);
  or or_7 (or_7_out, and_8_out, and_9_out, and_7_out, and_1_out);
  not not_3 (Q0_t, Q0);
  not not_4 (not_4_out, Q0);
  xor xor_1 (xor_1_out, Q0, Q1);
  and and_10 (and_10_out, Q0, Q1);
  _7_Segment_Display u_7_segment_display_1 (
    .g(or_4_out), .f(or_3_out), .a(or_1_out), .b(or_2_out), .e(or_6_out), .d(or_7_out), .c(or_5_out),
    .dp(1'b0));
  xor xor_2 (xor_2_out, and_10_out, Q2);
  and and_11 (and_11_out, Q1_t, Q0_t);
  and and_12 (and_12_out, Q1_t, Q0, Q2_t);
  and and_13 (and_13_out, Q2_t, Q0_t, Q1);
  and and_14 (and_14_out, Q1, Q0, Q2);
  and and_15 (and_15_out, Q1, Q0, Q2_t);
  and and_16 (and_16_out, Q1_t, Q0, Q2);
  and and_17 (and_17_out, Q0_t, Q1, Q2);
  LED YELLOW (.in(1'b0));
  LED GREEN (.in(1'b0));
  LED PURPLE (.in(1'b0));
  LED BLUE (.in(and_11_out));
  LED PINK (.in(and_12_out));
  LED ORANGE (.in(and_13_out));
  LED WHITE (.in(and_14_out));
  LED RED (.in(or_8_out));
  or or_8 (or_8_out, and_15_out, and_16_out, and_17_out);
endmodule
