// Logisim project synchronous_color_counter.circ as structural Verilog: 1 circuit, main circuit main
module main (
);

  wire and_1_out, and_2_out, and_3_out, and_4_out, and_5_out, and_6_out, and_7_out, and_8_out, clock_out,
       not_4_out, or_1_out, Q0, Q0_t, Q1, Q1_t, Q2, Q2_t, xor_1_out, xor_2_out;

  D_Flip_Flop D2 (.clk(clock_out), .D(xor_2_out), .Q(Q2));  // open: Qn, preset, en, reset
  not not_1 (Q2_t, Q2);
  Clock clock (.out(clock_out));
  not not_2 (Q1_t, Q1);
  D_Flip_Flop D1 (.clk(clock_out), .D(xor_1_out), .Q(Q1));  // open: Qn, preset, en, reset
  D_Flip_Flop D0 (.clk(clock_out), .D(not_4_out), .Q(Q0));  // open: Qn, preset, en, reset
  not not_3 (Q0_t, Q0);
  not not_4 (not_4_out, Q0);
  xor xor_1 (xor_1_out, Q0, Q1);
  and and_1 (and_1_out, Q0, Q1);
  xor xor_2 (xor_2_out, and_1_out, Q2);
  Hex_Digit_Display hex_digit_display_1 (.value({1'b0, Q2, Q1, Q0}));  // open: dp
  and and_2 (and_2_out, Q1_t, Q0_t);
  and and_3 (and_3_out, Q1_t, Q0, Q2_t);
  and and_4 (and_4_out, Q2_t, Q0_t, Q1);
  and and_5 (and_5_out, Q1, Q0, Q2);
  and and_6 (and_6_out, Q1, Q0, Q2_t);
  or or_1 (or_1_out, and_6_out, and_7_out, and_8_out);
  and and_7 (and_7_out, Q1_t, Q0, Q2);
  and and_8 (and_8_out, Q0_t, Q1, Q2);
  LED YELLOW (.in(1'b0));
  LED GREEN (.in(1'b0));
  LED PURPLE (.in(1'b0));
  LED BLUE (.in(and_2_out));
  LED PINK (.in(and_3_out));
  LED ORANGE (.in(and_4_out));
  LED WHITE (.in(and_5_out));
  LED RED (.in(or_1_out));
endmodule
